# Fritzing sketch RGBCalendar (saved by Fritzing 0.9.3b)

parts:
  LCD1 = LCD screen
  WeMos_D1_Mini1 = WeMos D1 Mini
  LCM1602_IIC1 = LCM1602 IIC [part_number="LCM1602 IIC" chip_label="LCM1602 IIC" package="DIP (Dual Inline) [THT]"]
  LED1 = RGB LED (com. cathode, rbg) [package="5 mm [THT]"]
  R1 = Resistor [tolerance=±5% resistance=220 package="0402 [SMD]"]
  R2 = Resistor [tolerance=±5% resistance=220 package="0402 [SMD]"]
  R3 = Resistor [tolerance=±5% resistance=220 package="0402 [SMD]"]

nets:
  VSS: LCD1.VSS, LCM1602_IIC1.VSS
  VDD: LCD1.VDD, LCM1602_IIC1.VDD
  N1: LCD1.V0, LCM1602_IIC1.V0
  N2: LCD1.RS, LCM1602_IIC1.RS
  N3: LCD1.R/W, LCM1602_IIC1.RW
  N4: LCD1.E, LCM1602_IIC1.E
  N5: LCD1.DB0, LCM1602_IIC1.D0
  N6: LCD1.DB1, LCM1602_IIC1.D1
  N7: LCD1.DB2, LCM1602_IIC1.D2
  N8: LCD1.DB3, LCM1602_IIC1.D3
  N9: LCD1.DB4, LCM1602_IIC1.D4
  N10: LCD1.DB5, LCM1602_IIC1.D5
  N11: LCD1.DB6, LCM1602_IIC1.D6
  N12: LCD1.DB7, LCM1602_IIC1.D7
  N13: LCD1.LED+, LCM1602_IIC1.A
  N14: LCD1.LED-, LCM1602_IIC1.K
  5V: WeMos_D1_Mini1.5V, LCM1602_IIC1.VCC
  N15: WeMos_D1_Mini1.D2, R1.Pin_0
  N16: WeMos_D1_Mini1.D3, R2.Pin_0
  N17: WeMos_D1_Mini1.D4, R3.Pin_0
  N18: WeMos_D1_Mini1.D5, LCM1602_IIC1.SDA
  N19: WeMos_D1_Mini1.D6, LCM1602_IIC1.SCL
  N20: WeMos_D1_Mini1.G, LCM1602_IIC1.GND, LED1.common_cathode
  N21: LED1.red_anode, R1.Pin_1
  N22: LED1.blue_anode, R2.Pin_1
  N23: LED1.green_anode, R3.Pin_1

custom parts:
  LCM1602 IIC: I2C-Module to use a 1602 or 2004 LCD on with the wire.h libory Serial LCD Modul
